# Fritzing sketch UNO-NodeMCU_Serial_Transmit_3Sensors_Node (saved by Fritzing 0.8.7b)

parts:
  U1 = NodeMCU V1.0
  Part1 = Arduino Uno (Rev3)
  AM1 = AM2320 Humidity and Temperature Sensor [part_number="Adafruit #3721"]
  AM2 = AM2320 Humidity and Temperature Sensor [part_number="Adafruit #3721"]
  AM3 = AM2320 Humidity and Temperature Sensor [part_number="Adafruit #3721"]
  R1 = Photocell (LDR) [package=THT]
  R2 = Photocell (LDR) [package=THT]
  R3 = Photocell (LDR) [package=THT]
  R4 = Resistor [tolerance=±5% resistance=220 package=THT]
  R6 = Resistor [tolerance=±5% resistance=220 package=THT]
  LED1 = LED - 5mm [color="Green (570nm)" package="5 mm [THT]"]
  LED2 = LED - 5mm [color="Yellow (585nm)" package="5 mm [THT]"]
  LED3 = smd LED [color="Red (635nm)" package="0805 [SMD]"]
  Part2 = FC-28 Soil Hygrometer Module
  Part3 = FC-28 Soil Hygrometer Module
  Part4 = FC-28 Soil Hygrometer Module - Probe
  Part5 = FC-28 Soil Hygrometer Module - Probe
  R7 = Resistor [tolerance=±5% resistance=220 package=THT]
  R8 = Resistor [tolerance=±5% resistance=220 package=THT]
  R9 = Resistor [tolerance=±5% resistance=220 package=THT]
  R5 = Resistor [tolerance=±5% resistance=220 package=THT]

nets:
  N1: U1.D1, Part1.D8
  N2: U1.D2, Part1.D9_PWM
  GND: U1.GND, Part1.GND, AM1.SCL, R7.Pin_0
  N3: U1.D7, LED2.anode
  N4: U1.D8, LED1.anode
  VIN: U1.Vin, Part1.VIN
  N5: Part1.A0, R1.pin_1, R4.Pin_0
  N6: Part1.A1, R2.pin_1, R6.Pin_0
  N7: Part1.A2, R3.pin_1, R5.Pin_0
  N8: Part1.A3, Part3.AO
  N9: Part1.A4/SDA, Part2.AO
  N10: Part1.D5_PWM, AM1.SDA
  N11: Part1.D6_PWM, AM2.SDA
  N12: Part1.D7, AM3.SDA
  5V: Part1.5V, AM1.VDD
  N13: LED1.cathode, R7.Pin_1
  N14: LED2.cathode, R8.Pin_1
  N15: LED3.cathode, R9.Pin_1
  N16: Part2.POS, Part4.POS
  N17: Part2.NEG, Part4.NEG
  N18: Part3.POS, Part5.POS
  N19: Part3.NEG, Part5.NEG

notes:
  Arduino UNO
  ESP8266-12(NODE MCU)
  DHT_1
  DHT_2
  DHT_3
  Soil_1
  Soil_2
  WiFi
  Online
  MQTT
  Online
  data Transmit

custom parts:
  NodeMCU V1.0: ESP8266 based NodeMCU
  AM2320 Humidity and Temperature Sensor: AM2320 I2C Humidity and Temperature Sensor
  FC-28 Soil Hygrometer Module: The FC-28 is a soil hygrometer module that uses the Texas Instruments LM393 comparator chip to provide an analog measurement of soil humidity. The digital output is high when soil moisture is over a certain threshold, as determined by adjusting the potentiometer.
  FC-28 Soil Hygrometer Module - Probe: The FC-28 is a soil hygrometer module that uses the Texas Instruments LM393 comparator chip to provide an analog measurement of soil humidity.
